# Fritzing sketch lowrider_scatch (saved by Fritzing 0.9.3b)
breadboards: 1

parts:
  Part1 = Arduino Nano (Rev3.0)
  VCC1 = Battery block 9V
  IC1 = L293D [package=THT]
  Part2 = Bluetooth HC-05 Macho
  M1 = DC Motor
  M2 = DC Motor

nets:
  GND: Part1.GND, VCC1.-, IC1.0V, Part2.GND
  N1: Part1.D2, Part2.RXD
  N2: Part1.D3, Part2.TXD
  N3: Part1.D5, IC1.In_4
  N4: Part1.D6, IC1.In_3
  N5: Part1.D10, IC1.In_1
  N6: Part1.D11/MOSI, IC1.In_2
  VIN: Part1.VIN, VCC1.+, IC1.Enable_1, IC1.+Vmotor, IC1.Enable_2, IC1.+V, Part2.VCC
  N7: IC1.Out_1_(_Controlled_by_Enable_1_), M2.pin_2
  N8: IC1.Out_2_(_Controlled_by_Enable_1_), M2.pin_1
  N9: IC1.Out_3_(_Controlled_by_Enable_2_), M1.pin_1
  N10: IC1.Out_4_(_Controlled_by_Enable_2_), M1.pin_2
