# Fritzing sketch rotary_enc_led (saved by Fritzing 0.9.3b)
breadboards: 1

parts:
  Part1 = Arduino Uno (Rev3) - ICSP
  SW1 = ENCODER_RGB_CA [package=encoder_led_3]
  R1 = Resistor [tolerance=±5% resistance=100 package="1206 [SMD]"]
  LED1 = smd LED [color="Red (633nm)" package="1206 [SMD]"]

nets:
  N1: Part1.D10_PWM/SS, LED1.cathode
  N2: Part1.D6_PWM, SW1.SW
  N3: Part1.5V, SW1.-R
  N4: Part1.GND, R1.Pin_1
  N5: R1.Pin_0, LED1.anode
